// Logisim project OZ-1.circ as structural Verilog: 10 circuits, main circuit OZ-1
module OZ_1 (
  output [7:0] ROM_block_1,
  output [7:0] ROM_block_2
);

  wire alu_1_cout, alu_1_nz, alu_1_z, and_1_out, and_2_out, and_3_out, and_4_out, and_5_out, and_6_out,
       and_7_out, and_8_out, and_9_out, and_10_out, CLK_out, condition_block_1_q, falling_edge_register_1_q6,
       falling_edge_register_1_q7, instruction_decoder_1_add_sub_op_sig,
       instruction_decoder_1_add_sub_sig__0_1, instruction_decoder_1_alu_cntl_0,
       instruction_decoder_1_alu_cntl_1, instruction_decoder_1_alu_is_using_a_number_from_ram,
       instruction_decoder_1_conditional__nz__sig, instruction_decoder_1_conditional__z__sig,
       instruction_decoder_1_cp_op__sig, instruction_decoder_1_data_bus_is_an_address_signifier,
       instruction_decoder_1_data_bus_isn_t_in_use__a_and_b_are_in_use__signifier,
       instruction_decoder_1_jp_op_sig, instruction_decoder_1_ld_a_sig, instruction_decoder_1_ld_b_sig,
       instruction_decoder_1_load_operation_uses_ram, instruction_decoder_1_pon_op_sig,
       jump_p_c_control_1_q0, jump_p_c_control_1_q1, jump_p_c_control_1_q2, jump_p_c_control_1_q3,
       jump_p_c_control_1_q4, jump_p_c_control_1_q5, jump_p_c_control_1_q6, jump_p_c_control_1_q7, not_1_out,
       not_2_out, not_3_out, not_4_out, or_1_out, or_2_out, or_3_out, or_4_out, or_5_out, pin_driver_1_q0,
       pin_driver_1_q1, pin_driver_1_q2, pin_driver_1_q3, pin_driver_1_q4, pin_driver_1_q5, pin_driver_1_q6,
       pin_driver_1_q7;
  wire [7:0] alu_1_register_a_data_out, controlled_buffer_1_out, instruction_decoder_1_db0,
       n3_1_mux_8_bit_1_q, ram_1_alu_data_out, ram_1_reg__a_data_out, register_a_1_alu_out,
       register_a_1_data_bus_out, register_a_1_ram_out, register_b_1_alu_out, register_b_1_data_bus_out,
       rising_edge_register_1_q0;

  Clock #(.highDuration(1), .lowDuration(1)) CLK (.out(CLK_out));
  Jump_P_C__Control jump_p_c_control_1 (
    .P_C__in(rising_edge_register_1_q0), .Data_bus_in(controlled_buffer_1_out), .Q7(jump_p_c_control_1_q7),
    .Q6(jump_p_c_control_1_q6), .Q5(jump_p_c_control_1_q5), .Q4(jump_p_c_control_1_q4),
    .Q3(jump_p_c_control_1_q3), .Q2(jump_p_c_control_1_q2), .Q1(jump_p_c_control_1_q1),
    .Q0(jump_p_c_control_1_q0), .No_jump(not_1_out), .Jump(instruction_decoder_1_jp_op_sig),
    .In_from_condition_block(condition_block_1_q));
  rising_edge_register rising_edge_register_1 (
    .A0(jump_p_c_control_1_q0), .A1(jump_p_c_control_1_q1), .A2(jump_p_c_control_1_q2),
    .A3(jump_p_c_control_1_q3), .A4(jump_p_c_control_1_q4), .A5(jump_p_c_control_1_q5),
    .A6(jump_p_c_control_1_q6), .A7(jump_p_c_control_1_q7), .write(CLK_out), .read(1'b1),
    .Q0(rising_edge_register_1_q0[0]), .Q1(rising_edge_register_1_q0[1]), .Q2(rising_edge_register_1_q0[2]),
    .Q3(rising_edge_register_1_q0[3]), .Q4(rising_edge_register_1_q0[4]), .Q5(rising_edge_register_1_q0[5]),
    .Q6(rising_edge_register_1_q0[6]), .Q7(rising_edge_register_1_q0[7]));
  ROM #(.addrWidth(8), .dataWidth(8)) rom_1 (.addr(rising_edge_register_1_q0), .data(ROM_block_1));  // open: sel
  not not_1 (not_1_out, instruction_decoder_1_jp_op_sig);
  ROM #(.addrWidth(8), .dataWidth(8)) rom_2 (.addr(rising_edge_register_1_q0), .data(ROM_block_2));  // open: sel
  Instruction_Decoder instruction_decoder_1 (
    .A15(ROM_block_1[7]), .A14(ROM_block_1[6]), .A13(ROM_block_1[5]), .A12(ROM_block_1[4]),
    .A11(ROM_block_1[3]), .A10(ROM_block_1[2]), .A9(ROM_block_1[1]), .A8(ROM_block_1[0]),
    .A7(ROM_block_2[7]), .A6(ROM_block_2[6]), .A5(ROM_block_2[5]), .A4(ROM_block_2[4]), .A3(ROM_block_2[3]),
    .A2(ROM_block_2[2]), .A1(ROM_block_2[1]), .A0(ROM_block_2[0]),
    .In_from_condition_block(condition_block_1_q), .PON_op_sig(instruction_decoder_1_pon_op_sig),
    .JP_op_sig(instruction_decoder_1_jp_op_sig), .ADD_SUB_sig__0_1(instruction_decoder_1_add_sub_sig__0_1),
    .DB7(instruction_decoder_1_db0[7]), .DB6(instruction_decoder_1_db0[6]),
    .DB5(instruction_decoder_1_db0[5]), .DB4(instruction_decoder_1_db0[4]),
    .DB3(instruction_decoder_1_db0[3]), .DB2(instruction_decoder_1_db0[2]),
    .DB1(instruction_decoder_1_db0[1]), .DB0(instruction_decoder_1_db0[0]),
    .Conditional__Z__sig(instruction_decoder_1_conditional__z__sig),
    .CP_op__sig(instruction_decoder_1_cp_op__sig),
    .Data_bus_isn_t_in_use__A_and_B_are_in_use__signifier(instruction_decoder_1_data_bus_isn_t_in_use__a_and_b_are_in_use__signifier),
    .Conditional__NZ__sig(instruction_decoder_1_conditional__nz__sig),
    .Data_bus_is_an_address_signifier(instruction_decoder_1_data_bus_is_an_address_signifier),
    .Load_operation_uses_RAM(instruction_decoder_1_load_operation_uses_ram),
    .ALU_cntl_1(instruction_decoder_1_alu_cntl_1),
    .ALU_is_using_a_number_from_RAM(instruction_decoder_1_alu_is_using_a_number_from_ram),
    .ALU_cntl_0(instruction_decoder_1_alu_cntl_0), .LD_B_sig(instruction_decoder_1_ld_b_sig),
    .LD_A_sig(instruction_decoder_1_ld_a_sig), .ADD_SUB_op_sig(instruction_decoder_1_add_sub_op_sig));  // open: Data_bus_is_a_number_signifier, ALU_is_in_use_sig
  assign controlled_buffer_1_out = not_2_out ? instruction_decoder_1_db0 : 8'bz;  // Controlled_Buffer controlled_buffer_1
  not not_2 (not_2_out, instruction_decoder_1_data_bus_isn_t_in_use__a_and_b_are_in_use__signifier);
  Register_B register_b_1 (
    .Data_bus_in(controlled_buffer_1_out), .Data_bus_out(register_b_1_data_bus_out),
    .ALU_out(register_b_1_alu_out), .In_from_condition_block(condition_block_1_q),
    .Write(instruction_decoder_1_ld_b_sig), .Read(or_1_out), .Data_bus_out_cntl(and_3_out),
    .ALU_out_cntl(and_2_out), .CLK(CLK_out));
  and and_1 (and_1_out, instruction_decoder_1_ld_a_sig, instruction_decoder_1_data_bus_isn_t_in_use__a_and_b_are_in_use__signifier);
  assign controlled_buffer_1_out = and_1_out ? register_b_1_data_bus_out : 8'bz;  // Controlled_Buffer controlled_buffer_2
  assign controlled_buffer_1_out = and_4_out ? register_a_1_data_bus_out : 8'bz;  // Controlled_Buffer controlled_buffer_3
  and and_2 (and_2_out, instruction_decoder_1_add_sub_op_sig, instruction_decoder_1_data_bus_isn_t_in_use__a_and_b_are_in_use__signifier);
  or or_1 (or_1_out, instruction_decoder_1_data_bus_isn_t_in_use__a_and_b_are_in_use__signifier, and_3_out);
  and and_3 (and_3_out, instruction_decoder_1_ld_a_sig, instruction_decoder_1_data_bus_isn_t_in_use__a_and_b_are_in_use__signifier);
  and and_4 (and_4_out, instruction_decoder_1_data_bus_isn_t_in_use__a_and_b_are_in_use__signifier, instruction_decoder_1_ld_b_sig);
  or or_2 (or_2_out, instruction_decoder_1_data_bus_isn_t_in_use__a_and_b_are_in_use__signifier, instruction_decoder_1_ld_b_sig);
  and and_5 (and_5_out, instruction_decoder_1_data_bus_is_an_address_signifier, instruction_decoder_1_load_operation_uses_ram);
  Pin_Driver pin_driver_1 (
    .CLK(CLK_out), .PON_op__sig__in(instruction_decoder_1_pon_op_sig), .CB_in(condition_block_1_q),
    .Data_bus_in(controlled_buffer_1_out), .Q7(pin_driver_1_q7), .Q6(pin_driver_1_q6), .Q5(pin_driver_1_q5),
    .Q4(pin_driver_1_q4), .Q3(pin_driver_1_q3), .Q2(pin_driver_1_q2), .Q1(pin_driver_1_q1),
    .Q0(pin_driver_1_q0));
  _7_Segment_Display u_7_segment_display_1 (
    .g(pin_driver_1_q7), .f(pin_driver_1_q6), .a(pin_driver_1_q5), .b(pin_driver_1_q4), .e(pin_driver_1_q3),
    .d(pin_driver_1_q2), .c(pin_driver_1_q1), .dp(pin_driver_1_q0));
  or or_3 (or_3_out, instruction_decoder_1_add_sub_op_sig, or_2_out, and_5_out);
  or or_4 (or_4_out, instruction_decoder_1_add_sub_op_sig, instruction_decoder_1_ld_a_sig, instruction_decoder_1_load_operation_uses_ram);
  falling_edge_register falling_edge_register_1 (
    .A5(alu_1_cout), .A6(alu_1_nz), .A7(alu_1_z), .enable(and_6_out), .read(1'b1),
    .Q6(falling_edge_register_1_q6), .Q7(falling_edge_register_1_q7));  // open: A0, A1, A2, A3, A4, Q0, Q1, Q2, Q3, Q4, Q5
  Register_A register_a_1 (
    .CP_sig_in(instruction_decoder_1_cp_op__sig), .Data_bus_in(controlled_buffer_1_out),
    .ALU_in(alu_1_register_a_data_out), .RAM_in(ram_1_reg__a_data_out),
    .Data_bus_out(register_a_1_data_bus_out), .ALU_out(register_a_1_alu_out), .RAM_out(register_a_1_ram_out),
    .In_from_condition_block(condition_block_1_q), .Data_bus_in_cntl(instruction_decoder_1_ld_a_sig),
    .ALU_in_cntl(instruction_decoder_1_add_sub_op_sig),
    .RAM_in_cntl(instruction_decoder_1_load_operation_uses_ram), .Write(or_4_out), .Read(or_3_out),
    .Data_bus_out_cntl(or_2_out), .ALU_out_cntl(instruction_decoder_1_add_sub_op_sig),
    .RAM_out_cntl(and_5_out), .CLK(CLK_out));
  Condition_Block condition_block_1 (
    .Z(falling_edge_register_1_q7), .NZ(falling_edge_register_1_q6),
    .test_Z(instruction_decoder_1_conditional__z__sig), .test_NZ(instruction_decoder_1_conditional__nz__sig),
    .Q(condition_block_1_q));
  and and_6 (and_6_out, CLK_out, instruction_decoder_1_add_sub_op_sig);
  ALU alu_1 (
    .Other_number_in(n3_1_mux_8_bit_1_q), .Register_A_in(register_a_1_alu_out), .NZ(alu_1_nz), .Z(alu_1_z),
    .Cout(alu_1_cout), .Register_A_data_out(alu_1_register_a_data_out),
    .Sub_Add_prime(instruction_decoder_1_add_sub_sig__0_1), .cntl1(instruction_decoder_1_alu_cntl_1),
    .cntl0(instruction_decoder_1_alu_cntl_0));
  RAM ram_1 (
    .Data_bus_in(controlled_buffer_1_out), .Register_A_in(register_a_1_ram_out),
    .ALU_data_out(ram_1_alu_data_out), .Reg__A_data_out(ram_1_reg__a_data_out), .CLK(CLK_out),
    .In_from_condition_block(condition_block_1_q), .Read(or_5_out), .Write(and_8_out),
    .ALU_out_cntl(instruction_decoder_1_alu_is_using_a_number_from_ram),
    .Register_A_out_cntl(instruction_decoder_1_load_operation_uses_ram));
  and and_7 (and_7_out, instruction_decoder_1_add_sub_op_sig, not_3_out);
  _3_1_MUX_8_bit u_3_1_mux_8_bit_1 (
    .C(controlled_buffer_1_out), .B(register_b_1_alu_out), .A(ram_1_alu_data_out), .Q(n3_1_mux_8_bit_1_q),
    .cntl2(and_7_out), .cntl1(and_9_out), .cntl0(instruction_decoder_1_alu_is_using_a_number_from_ram));
  and and_8 (and_8_out, instruction_decoder_1_load_operation_uses_ram, not_4_out);
  or or_5 (or_5_out, instruction_decoder_1_alu_is_using_a_number_from_ram, and_10_out);
  not not_3 (not_3_out, instruction_decoder_1_data_bus_isn_t_in_use__a_and_b_are_in_use__signifier);
  and and_9 (and_9_out, instruction_decoder_1_add_sub_op_sig, instruction_decoder_1_data_bus_isn_t_in_use__a_and_b_are_in_use__signifier);
  not not_4 (not_4_out, instruction_decoder_1_ld_a_sig);
  and and_10 (and_10_out, instruction_decoder_1_load_operation_uses_ram, instruction_decoder_1_ld_a_sig);

  // Notes on the sheet:
  //   Copyright - Ben Oztalay 2008-2009
  //   JP/P.C. Control
  //   Prgm Counter
  //   Instruction Decoder
  //   Register B
  //   Pin Driver
  //   Register A
  //   C.B.
  //   Flags Reg,
  //   ALU
  //   RAM
  //   3-1
endmodule

module Instruction_Decoder (
  input  A15,
  input  A14,
  input  A13,
  input  A12,
  input  A11,
  input  A10,
  input  A9,
  input  A8,
  input  A7,
  input  A6,
  input  A5,
  input  A4,
  input  A3,
  input  A2,
  input  A1,
  input  A0,
  input  In_from_condition_block,
  output DB7,
  output DB6,
  output DB5,
  output DB4,
  output DB3,
  output DB2,
  output DB1,
  output DB0,
  output Conditional__Z__sig,
  output Data_bus_is_a_number_signifier,
  output CP_op__sig,
  output Data_bus_isn_t_in_use__A_and_B_are_in_use__signifier,
  output JP_op_sig,
  output ADD_SUB_sig__0_1,
  output Conditional__NZ__sig,
  output Data_bus_is_an_address_signifier,
  output Load_operation_uses_RAM,
  output ALU_cntl_1,
  output ALU_is_using_a_number_from_RAM,
  output ALU_cntl_0,
  output PON_op_sig,
  output LD_B_sig,
  output LD_A_sig,
  output ALU_is_in_use_sig,
  output ADD_SUB_op_sig
);

  wire and_1_out, and_2_out, and_5_out, and_6_out, and_23_out, and_24_out, buffer_1_out, buffer_2_out,
       buffer_3_out, buffer_4_out, buffer_5_out, buffer_6_out, buffer_7_out, buffer_8_out, buffer_9_out,
       buffer_10_out, buffer_11_out, buffer_12_out, buffer_13_out, buffer_14_out, buffer_15_out,
       buffer_16_out, not_1_out, not_2_out, not_3_out, not_4_out, not_5_out, not_6_out, not_7_out, not_8_out,
       not_9_out, not_10_out, or_1_out, or_2_out, or_3_out, xor_2_out;

  not not_1 (not_1_out, buffer_2_out);
  not not_2 (not_2_out, buffer_3_out);
  and and_1 (and_1_out, not_2_out, not_1_out);
  xor xor_1 (JP_op_sig, buffer_3_out, ADD_SUB_sig__0_1);
  and and_2 (and_2_out, buffer_2_out, buffer_3_out);
  and and_3 (PON_op_sig, and_2_out, buffer_1_out, buffer_5_out);
  buf buffer_1 (buffer_1_out, A13);
  buf buffer_2 (buffer_2_out, A14);
  buf buffer_3 (buffer_3_out, A15);
  and and_4 (ADD_SUB_sig__0_1, buffer_3_out, buffer_2_out);
  xor xor_2 (xor_2_out, ADD_SUB_sig__0_1, buffer_2_out);
  not not_3 (not_3_out, ADD_SUB_sig__0_1);
  not not_4 (not_4_out, PON_op_sig);
  and and_5 (and_5_out, not_4_out, not_5_out);
  not not_5 (not_5_out, JP_op_sig);
  buf buffer_4 (buffer_4_out, A11);
  buf buffer_5 (buffer_5_out, A12);
  and and_6 (and_6_out, and_1_out, or_1_out);
  or or_1 (or_1_out, not_3_out, ADD_SUB_sig__0_1);
  not not_6 (not_6_out, xor_2_out);
  buf buffer_6 (buffer_6_out, A10);
  buf buffer_7 (buffer_7_out, A8);
  buf buffer_8 (buffer_8_out, A9);
  and and_7 (CP_op__sig, buffer_6_out, buffer_4_out);
  and and_8 (ALU_cntl_1, buffer_5_out, and_6_out);
  and and_9 (ALU_cntl_0, buffer_1_out, and_6_out);
  and and_10 (LD_B_sig, buffer_5_out, xor_2_out);
  and and_11 (LD_A_sig, buffer_1_out, xor_2_out);
  and and_12 (ALU_is_in_use_sig, not_6_out, or_1_out, and_5_out);
  not not_7 (not_7_out, ADD_SUB_sig__0_1);
  or or_2 (or_2_out, not_7_out, ADD_SUB_sig__0_1);
  buf buffer_9 (buffer_9_out, A5);
  buf buffer_10 (buffer_10_out, A7);
  buf buffer_11 (buffer_11_out, A6);
  and and_13 (DB6, buffer_11_out, and_23_out);
  and and_14 (DB7, buffer_10_out, and_23_out);
  xor xor_3 (Conditional__Z__sig, buffer_6_out, CP_op__sig);
  xor xor_4 (Conditional__NZ__sig, CP_op__sig, buffer_4_out);
  and and_15 (ADD_SUB_op_sig, ALU_is_in_use_sig, or_2_out);
  buf buffer_12 (buffer_12_out, A3);
  buf buffer_13 (buffer_13_out, A4);
  and and_16 (DB3, buffer_12_out, and_23_out);
  and and_17 (DB4, buffer_13_out, and_23_out);
  and and_18 (DB5, buffer_9_out, and_23_out);
  buf buffer_14 (buffer_14_out, A1);
  buf buffer_15 (buffer_15_out, A0);
  buf buffer_16 (buffer_16_out, A2);
  and and_19 (DB0, buffer_15_out, and_23_out);
  and and_20 (DB1, buffer_14_out, and_23_out);
  and and_21 (DB2, buffer_16_out, and_23_out);
  and and_22 (Data_bus_isn_t_in_use__A_and_B_are_in_use__signifier, buffer_7_out, buffer_8_out);
  not not_8 (not_8_out, xor_2_out);
  not not_9 (not_9_out, JP_op_sig);
  not not_10 (not_10_out, Data_bus_isn_t_in_use__A_and_B_are_in_use__signifier);
  and and_23 (and_23_out, In_from_condition_block, not_10_out, or_3_out);
  xor xor_5 (Data_bus_is_a_number_signifier, buffer_7_out, Data_bus_isn_t_in_use__A_and_B_are_in_use__signifier);
  xor xor_6 (Data_bus_is_an_address_signifier, Data_bus_isn_t_in_use__A_and_B_are_in_use__signifier, buffer_8_out);
  and and_24 (and_24_out, not_8_out, not_9_out);
  or or_3 (or_3_out, Data_bus_is_a_number_signifier, Data_bus_is_an_address_signifier);
  and and_25 (Load_operation_uses_RAM, Data_bus_is_an_address_signifier, xor_2_out);
  and and_26 (ALU_is_using_a_number_from_RAM, Data_bus_is_an_address_signifier, and_24_out, or_1_out);

  // Notes on the sheet:
  //   Instruction Bits
  //   Copyright - Ben Oztalay 2008-2009
endmodule

module ALU (
  input  [7:0] Other_number_in,
  input  [7:0] Register_A_in,
  input  Sub_Add_prime,
  input  cntl1,
  input  cntl0,
  output NZ,
  output Z,
  output Cout,
  output [7:0] Register_A_data_out
);

  wire and_1_out, and_2_out, and_4_out, and_5_out, and_6_out, and_7_out, and_8_out, and_9_out,
       full_adder_1_s, full_adder_2_cout, full_adder_2_s, full_adder_3_cout, full_adder_3_s,
       full_adder_4_cout, full_adder_4_s, full_adder_5_cout, full_adder_5_s, full_adder_6_cout,
       full_adder_6_s, full_adder_7_cout, full_adder_7_s, full_adder_8_cout, full_adder_8_s, n1x2_mux_1_q0,
       n1x2_mux_2_q0, n1x2_mux_3_q0, n1x2_mux_4_q0, n1x2_mux_5_q0, n1x2_mux_6_q0, n1x2_mux_7_q0,
       n1x2_mux_8_q0, not_1_out, not_2_out, not_3_out, not_4_out, not_5_out, not_6_out, not_7_out, not_8_out,
       not_9_out, not_10_out, not_12_out, not_13_out, not_14_out, not_15_out, not_16_out, not_17_out,
       or_1_out, or_2_out, or_3_out, or_4_out, or_5_out, or_6_out, or_7_out, or_8_out, xor_1_out, xor_2_out,
       xor_3_out, xor_4_out, xor_5_out, xor_6_out, xor_7_out, xor_8_out;

  xor xor_1 (xor_1_out, Other_number_in[7], Register_A_in[7]);
  not not_1 (not_1_out, Other_number_in[7]);
  _1x2_MUX u_1x2_mux_1 (.A0(Other_number_in[7]), .A1(not_1_out), .sel(Sub_Add_prime), .Q0(n1x2_mux_1_q0));
  full_adder full_adder_1 (
    .Cout(Cout), .A(n1x2_mux_1_q0), .B(Register_A_in[7]), .S(full_adder_1_s), .Cin(full_adder_2_cout));
  or or_1 (or_1_out, Other_number_in[7], Register_A_in[7]);
  and and_1 (and_1_out, Other_number_in[7], Register_A_in[7]);
  _2x4_MUX u_2x4_mux_1 (
    .A0(full_adder_1_s), .A1(and_1_out), .A2(or_1_out), .A3(xor_1_out), .cntl1(cntl1), .cntl0(cntl0),
    .Q0(Register_A_data_out[7]));
  not not_2 (not_2_out, Register_A_data_out[6]);
  not not_3 (not_3_out, Register_A_data_out[5]);
  not not_4 (not_4_out, Register_A_data_out[7]);
  not not_5 (not_5_out, Register_A_data_out[4]);
  not not_6 (not_6_out, Other_number_in[6]);
  or or_2 (or_2_out, Other_number_in[6], Register_A_in[6]);
  xor xor_2 (xor_2_out, Other_number_in[6], Register_A_in[6]);
  and and_2 (and_2_out, Other_number_in[6], Register_A_in[6]);
  not not_7 (not_7_out, Register_A_data_out[2]);
  not not_8 (not_8_out, Register_A_data_out[1]);
  not not_9 (not_9_out, Register_A_data_out[0]);
  not not_10 (not_10_out, Register_A_data_out[3]);
  and and_3 (Z, not_4_out, not_2_out, not_3_out, not_5_out, not_10_out, not_7_out, not_8_out, not_9_out);
  not not_11 (NZ, Z);
  _1x2_MUX u_1x2_mux_2 (.A0(Other_number_in[6]), .A1(not_6_out), .sel(Sub_Add_prime), .Q0(n1x2_mux_2_q0));
  full_adder full_adder_2 (
    .Cout(full_adder_2_cout), .A(n1x2_mux_2_q0), .B(Register_A_in[6]), .S(full_adder_2_s),
    .Cin(full_adder_3_cout));
  xor xor_3 (xor_3_out, Other_number_in[5], Register_A_in[5]);
  _2x4_MUX u_2x4_mux_2 (
    .A0(full_adder_2_s), .A1(and_2_out), .A2(or_2_out), .A3(xor_2_out), .cntl1(cntl1), .cntl0(cntl0),
    .Q0(Register_A_data_out[6]));
  not not_12 (not_12_out, Other_number_in[5]);
  _1x2_MUX u_1x2_mux_3 (.A0(Other_number_in[5]), .A1(not_12_out), .sel(Sub_Add_prime), .Q0(n1x2_mux_3_q0));
  full_adder full_adder_3 (
    .Cout(full_adder_3_cout), .A(n1x2_mux_3_q0), .B(Register_A_in[5]), .S(full_adder_3_s),
    .Cin(full_adder_4_cout));
  or or_3 (or_3_out, Other_number_in[5], Register_A_in[5]);
  and and_4 (and_4_out, Other_number_in[5], Register_A_in[5]);
  _2x4_MUX u_2x4_mux_3 (
    .A0(full_adder_3_s), .A1(and_4_out), .A2(or_3_out), .A3(xor_3_out), .cntl1(cntl1), .cntl0(cntl0),
    .Q0(Register_A_data_out[5]));
  not not_13 (not_13_out, Other_number_in[4]);
  and and_5 (and_5_out, Other_number_in[4], Register_A_in[4]);
  or or_4 (or_4_out, Other_number_in[4], Register_A_in[4]);
  xor xor_4 (xor_4_out, Other_number_in[4], Register_A_in[4]);
  _1x2_MUX u_1x2_mux_4 (.A0(Other_number_in[4]), .A1(not_13_out), .sel(Sub_Add_prime), .Q0(n1x2_mux_4_q0));
  full_adder full_adder_4 (
    .Cout(full_adder_4_cout), .A(n1x2_mux_4_q0), .B(Register_A_in[4]), .S(full_adder_4_s),
    .Cin(full_adder_5_cout));
  xor xor_5 (xor_5_out, Other_number_in[3], Register_A_in[3]);
  _2x4_MUX u_2x4_mux_4 (
    .A0(full_adder_4_s), .A1(and_5_out), .A2(or_4_out), .A3(xor_4_out), .cntl1(cntl1), .cntl0(cntl0),
    .Q0(Register_A_data_out[4]));
  not not_14 (not_14_out, Other_number_in[3]);
  _1x2_MUX u_1x2_mux_5 (.A0(Other_number_in[3]), .A1(not_14_out), .sel(Sub_Add_prime), .Q0(n1x2_mux_5_q0));
  full_adder full_adder_5 (
    .Cout(full_adder_5_cout), .A(n1x2_mux_5_q0), .B(Register_A_in[3]), .S(full_adder_5_s),
    .Cin(full_adder_6_cout));
  and and_6 (and_6_out, Other_number_in[3], Register_A_in[3]);
  or or_5 (or_5_out, Other_number_in[3], Register_A_in[3]);
  _2x4_MUX u_2x4_mux_5 (
    .A0(full_adder_5_s), .A1(and_6_out), .A2(or_5_out), .A3(xor_5_out), .cntl1(cntl1), .cntl0(cntl0),
    .Q0(Register_A_data_out[3]));
  not not_15 (not_15_out, Other_number_in[2]);
  xor xor_6 (xor_6_out, Other_number_in[2], Register_A_in[2]);
  and and_7 (and_7_out, Other_number_in[2], Register_A_in[2]);
  or or_6 (or_6_out, Other_number_in[2], Register_A_in[2]);
  _1x2_MUX u_1x2_mux_6 (.A0(Other_number_in[2]), .A1(not_15_out), .sel(Sub_Add_prime), .Q0(n1x2_mux_6_q0));
  full_adder full_adder_6 (
    .Cout(full_adder_6_cout), .A(n1x2_mux_6_q0), .B(Register_A_in[2]), .S(full_adder_6_s),
    .Cin(full_adder_7_cout));
  xor xor_7 (xor_7_out, Other_number_in[1], Register_A_in[1]);
  _2x4_MUX u_2x4_mux_6 (
    .A0(full_adder_6_s), .A1(and_7_out), .A2(or_6_out), .A3(xor_6_out), .cntl1(cntl1), .cntl0(cntl0),
    .Q0(Register_A_data_out[2]));
  not not_16 (not_16_out, Other_number_in[1]);
  _1x2_MUX u_1x2_mux_7 (.A0(Other_number_in[1]), .A1(not_16_out), .sel(Sub_Add_prime), .Q0(n1x2_mux_7_q0));
  full_adder full_adder_7 (
    .Cout(full_adder_7_cout), .A(n1x2_mux_7_q0), .B(Register_A_in[1]), .S(full_adder_7_s),
    .Cin(full_adder_8_cout));
  and and_8 (and_8_out, Other_number_in[1], Register_A_in[1]);
  or or_7 (or_7_out, Other_number_in[1], Register_A_in[1]);
  _2x4_MUX u_2x4_mux_7 (
    .A0(full_adder_7_s), .A1(and_8_out), .A2(or_7_out), .A3(xor_7_out), .cntl1(cntl1), .cntl0(cntl0),
    .Q0(Register_A_data_out[1]));
  not not_17 (not_17_out, Other_number_in[0]);
  xor xor_8 (xor_8_out, Other_number_in[0], Register_A_in[0]);
  and and_9 (and_9_out, Other_number_in[0], Register_A_in[0]);
  or or_8 (or_8_out, Other_number_in[0], Register_A_in[0]);
  _1x2_MUX u_1x2_mux_8 (.A0(Other_number_in[0]), .A1(not_17_out), .sel(Sub_Add_prime), .Q0(n1x2_mux_8_q0));
  full_adder full_adder_8 (
    .Cout(full_adder_8_cout), .A(n1x2_mux_8_q0), .B(Register_A_in[0]), .S(full_adder_8_s), .Cin(Sub_Add_prime));
  _2x4_MUX u_2x4_mux_8 (
    .A0(full_adder_8_s), .A1(and_9_out), .A2(or_8_out), .A3(xor_8_out), .cntl1(cntl1), .cntl0(cntl0),
    .Q0(Register_A_data_out[0]));

  // Notes on the sheet:
  //   2 X 4
  //   2 X 4
  //   2 X 4
  //   Copyright - Ben Oztalay 2008-2009
  //   2 X 4
  //   2 X 4
  //   2 X 4
  //   2 X 4
endmodule

module Register_File (
  input  A7,
  input  A6,
  input  A5,
  input  A4,
  input  A3,
  input  A2,
  input  A1,
  input  A0,
  input  W,
  input  R,
  input  Wa1,
  input  Wa0,
  input  Ra1,
  input  Ra0,
  output Q7,
  output Q6,
  output Q5,
  output Q4,
  output Q3,
  output Q2,
  output Q1,
  output Q0
);

  wire and_1_out, and_2_out, and_3_out, and_4_out, and_5_out, and_6_out, and_7_out, and_8_out,
       falling_edge_register_1_q0, falling_edge_register_1_q1, falling_edge_register_1_q2,
       falling_edge_register_1_q3, falling_edge_register_1_q4, falling_edge_register_1_q5,
       falling_edge_register_1_q6, falling_edge_register_1_q7, falling_edge_register_2_q0,
       falling_edge_register_2_q1, falling_edge_register_2_q2, falling_edge_register_2_q3,
       falling_edge_register_2_q4, falling_edge_register_2_q5, falling_edge_register_2_q6,
       falling_edge_register_2_q7, falling_edge_register_3_q0, falling_edge_register_3_q1,
       falling_edge_register_3_q2, falling_edge_register_3_q3, falling_edge_register_3_q4,
       falling_edge_register_3_q5, falling_edge_register_3_q6, falling_edge_register_3_q7,
       falling_edge_register_4_q0, falling_edge_register_4_q1, falling_edge_register_4_q2,
       falling_edge_register_4_q3, falling_edge_register_4_q4, falling_edge_register_4_q5,
       falling_edge_register_4_q6, falling_edge_register_4_q7, n1_of_4_1_q0, n1_of_4_1_q1, n1_of_4_1_q2,
       n1_of_4_1_q3, n1_of_4_2_q0, n1_of_4_2_q1, n1_of_4_2_q2, n1_of_4_2_q3, n8_32_splitter_1_q00,
       n8_32_splitter_1_q01, n8_32_splitter_1_q02, n8_32_splitter_1_q03, n8_32_splitter_1_q04,
       n8_32_splitter_1_q05, n8_32_splitter_1_q06, n8_32_splitter_1_q07, n8_32_splitter_1_q10,
       n8_32_splitter_1_q11, n8_32_splitter_1_q12, n8_32_splitter_1_q13, n8_32_splitter_1_q14,
       n8_32_splitter_1_q15, n8_32_splitter_1_q16, n8_32_splitter_1_q17, n8_32_splitter_1_q20,
       n8_32_splitter_1_q21, n8_32_splitter_1_q22, n8_32_splitter_1_q23, n8_32_splitter_1_q24,
       n8_32_splitter_1_q25, n8_32_splitter_1_q26, n8_32_splitter_1_q27, n8_32_splitter_1_q30,
       n8_32_splitter_1_q31, n8_32_splitter_1_q32, n8_32_splitter_1_q33, n8_32_splitter_1_q34,
       n8_32_splitter_1_q35, n8_32_splitter_1_q36, n8_32_splitter_1_q37;

  and and_1 (and_1_out, n1_of_4_2_q3, R);
  and and_2 (and_2_out, n1_of_4_1_q3, W);
  falling_edge_register falling_edge_register_1 (
    .A0(n8_32_splitter_1_q30), .A1(n8_32_splitter_1_q31), .A2(n8_32_splitter_1_q32),
    .A3(n8_32_splitter_1_q33), .A4(n8_32_splitter_1_q34), .A5(n8_32_splitter_1_q35),
    .A6(n8_32_splitter_1_q36), .A7(n8_32_splitter_1_q37), .enable(and_2_out), .read(and_1_out),
    .Q0(falling_edge_register_1_q0), .Q1(falling_edge_register_1_q1), .Q2(falling_edge_register_1_q2),
    .Q3(falling_edge_register_1_q3), .Q4(falling_edge_register_1_q4), .Q5(falling_edge_register_1_q5),
    .Q6(falling_edge_register_1_q6), .Q7(falling_edge_register_1_q7));
  and and_3 (and_3_out, n1_of_4_1_q2, W);
  and and_4 (and_4_out, n1_of_4_2_q2, R);
  _8_4_input_OR_gates u_8_4_input_or_gates_1 (
    .D7(falling_edge_register_1_q7), .D6(falling_edge_register_1_q6), .D5(falling_edge_register_1_q5),
    .D4(falling_edge_register_1_q4), .D3(falling_edge_register_1_q3), .D2(falling_edge_register_1_q2),
    .D1(falling_edge_register_1_q1), .D0(falling_edge_register_1_q0), .C7(falling_edge_register_2_q7),
    .C6(falling_edge_register_2_q6), .C5(falling_edge_register_2_q5), .C4(falling_edge_register_2_q4),
    .C3(falling_edge_register_2_q3), .C2(falling_edge_register_2_q2), .C1(falling_edge_register_2_q1),
    .C0(falling_edge_register_2_q0), .B7(falling_edge_register_3_q7), .B6(falling_edge_register_3_q6),
    .B5(falling_edge_register_3_q5), .B4(falling_edge_register_3_q4), .B3(falling_edge_register_3_q3),
    .B2(falling_edge_register_3_q2), .B1(falling_edge_register_3_q1), .B0(falling_edge_register_3_q0),
    .A7(falling_edge_register_4_q7), .A6(falling_edge_register_4_q6), .A5(falling_edge_register_4_q5),
    .A4(falling_edge_register_4_q4), .A3(falling_edge_register_4_q3), .A2(falling_edge_register_4_q2),
    .A1(falling_edge_register_4_q1), .A0(falling_edge_register_4_q0), .Q7(Q7), .Q6(Q6), .Q5(Q5), .Q4(Q4),
    .Q3(Q3), .Q2(Q2), .Q1(Q1), .Q0(Q0));
  _8_32_splitter u_8_32_splitter_1 (
    .A7(A7), .A6(A6), .A5(A5), .A4(A4), .A3(A3), .A2(A2), .A1(A1), .A0(A0), .Q37(n8_32_splitter_1_q37),
    .Q36(n8_32_splitter_1_q36), .Q35(n8_32_splitter_1_q35), .Q34(n8_32_splitter_1_q34),
    .Q33(n8_32_splitter_1_q33), .Q32(n8_32_splitter_1_q32), .Q31(n8_32_splitter_1_q31),
    .Q30(n8_32_splitter_1_q30), .Q27(n8_32_splitter_1_q27), .Q26(n8_32_splitter_1_q26),
    .Q25(n8_32_splitter_1_q25), .Q24(n8_32_splitter_1_q24), .Q23(n8_32_splitter_1_q23),
    .Q22(n8_32_splitter_1_q22), .Q21(n8_32_splitter_1_q21), .Q20(n8_32_splitter_1_q20),
    .Q17(n8_32_splitter_1_q17), .Q16(n8_32_splitter_1_q16), .Q15(n8_32_splitter_1_q15),
    .Q14(n8_32_splitter_1_q14), .Q13(n8_32_splitter_1_q13), .Q12(n8_32_splitter_1_q12),
    .Q11(n8_32_splitter_1_q11), .Q10(n8_32_splitter_1_q10), .Q07(n8_32_splitter_1_q07),
    .Q06(n8_32_splitter_1_q06), .Q05(n8_32_splitter_1_q05), .Q04(n8_32_splitter_1_q04),
    .Q03(n8_32_splitter_1_q03), .Q02(n8_32_splitter_1_q02), .Q01(n8_32_splitter_1_q01),
    .Q00(n8_32_splitter_1_q00));
  and and_5 (and_5_out, n1_of_4_1_q1, W);
  falling_edge_register falling_edge_register_2 (
    .A0(n8_32_splitter_1_q20), .A1(n8_32_splitter_1_q21), .A2(n8_32_splitter_1_q22),
    .A3(n8_32_splitter_1_q23), .A4(n8_32_splitter_1_q24), .A5(n8_32_splitter_1_q25),
    .A6(n8_32_splitter_1_q26), .A7(n8_32_splitter_1_q27), .enable(and_3_out), .read(and_4_out),
    .Q0(falling_edge_register_2_q0), .Q1(falling_edge_register_2_q1), .Q2(falling_edge_register_2_q2),
    .Q3(falling_edge_register_2_q3), .Q4(falling_edge_register_2_q4), .Q5(falling_edge_register_2_q5),
    .Q6(falling_edge_register_2_q6), .Q7(falling_edge_register_2_q7));
  and and_6 (and_6_out, n1_of_4_2_q1, R);
  falling_edge_register falling_edge_register_3 (
    .A0(n8_32_splitter_1_q10), .A1(n8_32_splitter_1_q11), .A2(n8_32_splitter_1_q12),
    .A3(n8_32_splitter_1_q13), .A4(n8_32_splitter_1_q14), .A5(n8_32_splitter_1_q15),
    .A6(n8_32_splitter_1_q16), .A7(n8_32_splitter_1_q17), .enable(and_5_out), .read(and_6_out),
    .Q0(falling_edge_register_3_q0), .Q1(falling_edge_register_3_q1), .Q2(falling_edge_register_3_q2),
    .Q3(falling_edge_register_3_q3), .Q4(falling_edge_register_3_q4), .Q5(falling_edge_register_3_q5),
    .Q6(falling_edge_register_3_q6), .Q7(falling_edge_register_3_q7));
  and and_7 (and_7_out, n1_of_4_2_q0, R);
  and and_8 (and_8_out, n1_of_4_1_q0, W);
  falling_edge_register falling_edge_register_4 (
    .A0(n8_32_splitter_1_q00), .A1(n8_32_splitter_1_q01), .A2(n8_32_splitter_1_q02),
    .A3(n8_32_splitter_1_q03), .A4(n8_32_splitter_1_q04), .A5(n8_32_splitter_1_q05),
    .A6(n8_32_splitter_1_q06), .A7(n8_32_splitter_1_q07), .enable(and_8_out), .read(and_7_out),
    .Q0(falling_edge_register_4_q0), .Q1(falling_edge_register_4_q1), .Q2(falling_edge_register_4_q2),
    .Q3(falling_edge_register_4_q3), .Q4(falling_edge_register_4_q4), .Q5(falling_edge_register_4_q5),
    .Q6(falling_edge_register_4_q6), .Q7(falling_edge_register_4_q7));
  _1_of_4 u_1_of_4_1 (.A1(Wa1), .A0(Wa0), .Q3(n1_of_4_1_q3), .Q2(n1_of_4_1_q2), .Q1(n1_of_4_1_q1), .Q0(n1_of_4_1_q0));
  _1_of_4 u_1_of_4_2 (.A1(Ra1), .A0(Ra0), .Q3(n1_of_4_2_q3), .Q2(n1_of_4_2_q2), .Q1(n1_of_4_2_q1), .Q0(n1_of_4_2_q0));

  // Notes on the sheet:
  //   Copyright - Ben Oztalay 2008-2009
endmodule

module Register_A (
  input  CP_sig_in,
  input  [7:0] Data_bus_in,
  input  [7:0] ALU_in,
  input  [7:0] RAM_in,
  input  In_from_condition_block,
  input  Data_bus_in_cntl,
  input  ALU_in_cntl,
  input  RAM_in_cntl,
  input  Write,
  input  Read,
  input  Data_bus_out_cntl,
  input  ALU_out_cntl,
  input  RAM_out_cntl,
  input  CLK,
  output [7:0] Data_bus_out,
  output [7:0] ALU_out,
  output [7:0] RAM_out
);

  wire and_1_out, and_2_out, and_3_out, and_4_out, and_5_out, and_6_out, and_7_out, and_8_out, not_1_out,
       not_2_out;
  wire [7:0] controlled_buffer_1_out, n3_1_mux_8_bit_1_q, register_1_q;

  Register #(.width(8)) register_1 (.D(n3_1_mux_8_bit_1_q), .Q(register_1_q), .clk(and_1_out));  // open: en, clr
  _3_1_MUX_8_bit u_3_1_mux_8_bit_1 (
    .C(Data_bus_in), .B(ALU_in), .A(RAM_in), .Q(n3_1_mux_8_bit_1_q), .cntl2(and_3_out), .cntl1(and_4_out),
    .cntl0(and_5_out));
  assign controlled_buffer_1_out = and_2_out ? register_1_q : 8'bz;  // Controlled_Buffer controlled_buffer_1
  _1_3_MUX_8_bit u_1_3_mux_8_bit_1 (
    .A(controlled_buffer_1_out), .Q2(Data_bus_out), .Q1(ALU_out), .Q0(RAM_out), .cntl2(and_6_out),
    .cntl1(and_7_out), .cntl0(and_8_out));
  and and_1 (and_1_out, Write, In_from_condition_block, not_2_out, not_1_out);
  and and_2 (and_2_out, In_from_condition_block, Read);
  not not_1 (not_1_out, CP_sig_in);
  and and_3 (and_3_out, In_from_condition_block, Data_bus_in_cntl);
  and and_4 (and_4_out, In_from_condition_block, ALU_in_cntl);
  and and_5 (and_5_out, In_from_condition_block, RAM_in_cntl);
  and and_6 (and_6_out, In_from_condition_block, Data_bus_out_cntl);
  and and_7 (and_7_out, In_from_condition_block, ALU_out_cntl);
  and and_8 (and_8_out, In_from_condition_block, RAM_out_cntl);
  not not_2 (not_2_out, CLK);

  // Notes on the sheet:
  //   Copyright - Ben Oztalay 2008-2009
endmodule

module Register_B (
  input  [7:0] Data_bus_in,
  input  In_from_condition_block,
  input  Write,
  input  Read,
  input  Data_bus_out_cntl,
  input  ALU_out_cntl,
  input  CLK,
  output [7:0] Data_bus_out,
  output [7:0] ALU_out
);

  wire and_9_out, and_10_out, not_1_out;
  wire [7:0] and_7_out, controlled_buffer_1_out, register_1_q;

  and and_1 (and_7_out[7], In_from_condition_block, Data_bus_in[7], Write);
  and and_2 (and_7_out[4], In_from_condition_block, Data_bus_in[4], Write);
  and and_3 (and_7_out[5], In_from_condition_block, Data_bus_in[5], Write);
  and and_4 (and_7_out[6], In_from_condition_block, Data_bus_in[6], Write);
  Register #(.width(8)) register_1 (.D(and_7_out), .Q(register_1_q), .clk(and_9_out));  // open: en, clr
  assign controlled_buffer_1_out = and_10_out ? register_1_q : 8'bz;  // Controlled_Buffer controlled_buffer_1
  and and_5 (and_7_out[2], In_from_condition_block, Data_bus_in[2], Write);
  and and_6 (and_7_out[3], In_from_condition_block, Data_bus_in[3], Write);
  and and_7 (and_7_out[0], In_from_condition_block, Data_bus_in[0], Write);
  and and_8 (and_7_out[1], In_from_condition_block, Data_bus_in[1], Write);
  and and_9 (and_9_out, In_from_condition_block, Write, not_1_out);
  and and_10 (and_10_out, In_from_condition_block, Read);
  _8_16_DEMUX u_8_16_demux_1 (
    .A7(controlled_buffer_1_out[7]), .A6(controlled_buffer_1_out[6]), .A5(controlled_buffer_1_out[5]),
    .A4(controlled_buffer_1_out[4]), .A3(controlled_buffer_1_out[3]), .A2(controlled_buffer_1_out[2]),
    .A1(controlled_buffer_1_out[1]), .A0(controlled_buffer_1_out[0]), .Q17(Data_bus_out[7]),
    .Q16(Data_bus_out[6]), .Q15(Data_bus_out[5]), .Q14(Data_bus_out[4]), .Q13(Data_bus_out[3]),
    .Q12(Data_bus_out[2]), .Q11(Data_bus_out[1]), .Q10(Data_bus_out[0]), .Q07(ALU_out[7]), .Q06(ALU_out[6]),
    .Q05(ALU_out[5]), .Q04(ALU_out[4]), .Q03(ALU_out[3]), .Q02(ALU_out[2]), .Q01(ALU_out[1]),
    .Q00(ALU_out[0]), .cntl1(Data_bus_out_cntl), .cntl0(ALU_out_cntl));
  not not_1 (not_1_out, CLK);

  // Notes on the sheet:
  //   Copyright - Ben Oztalay 2008-2009
endmodule

module RAM (
  input  [7:0] Register_A_in,
  input  [7:0] Data_bus_in,
  input  CLK,
  input  In_from_condition_block,
  input  Read,
  input  Write,
  input  ALU_out_cntl,
  input  Register_A_out_cntl,
  output [7:0] ALU_data_out,
  output [7:0] Reg__A_data_out
);

  wire and_1_out, and_2_out, and_3_out, and_4_out, and_5_out, controlled_buffer_4_out, not_1_out, not_2_out,
       not_3_out, or_1_out, or_2_out;
  wire [7:0] controlled_buffer_1_out, controlled_buffer_3_out, ram_1_data;

  assign controlled_buffer_1_out = In_from_condition_block ? Data_bus_in : 8'bz;  // Controlled_Buffer controlled_buffer_1
  RAM_part #(.addrWidth(8), .dataWidth(8)) ram_1 (
    .addr(controlled_buffer_1_out), .data(ram_1_data), .clk(and_1_out), .ld(or_1_out));  // open: sel, clr
  and and_1 (and_1_out, not_1_out, Write);
  or or_1 (or_1_out, and_2_out, Read);
  _8_16_DEMUX u_8_16_demux_1 (
    .A7(ram_1_data[7]), .A6(ram_1_data[6]), .A5(ram_1_data[5]), .A4(ram_1_data[4]), .A3(ram_1_data[3]),
    .A2(ram_1_data[2]), .A1(ram_1_data[1]), .A0(ram_1_data[0]), .Q17(ALU_data_out[7]), .Q16(ALU_data_out[6]),
    .Q15(ALU_data_out[5]), .Q14(ALU_data_out[4]), .Q13(ALU_data_out[3]), .Q12(ALU_data_out[2]),
    .Q11(ALU_data_out[1]), .Q10(ALU_data_out[0]), .Q07(Reg__A_data_out[7]), .Q06(Reg__A_data_out[6]),
    .Q05(Reg__A_data_out[5]), .Q04(Reg__A_data_out[4]), .Q03(Reg__A_data_out[3]), .Q02(Reg__A_data_out[2]),
    .Q01(Reg__A_data_out[1]), .Q00(Reg__A_data_out[0]), .cntl1(and_3_out), .cntl0(and_4_out));
  assign ram_1_data = controlled_buffer_4_out ? controlled_buffer_3_out : 8'bz;  // Controlled_Buffer controlled_buffer_2
  not not_1 (not_1_out, CLK);
  or or_2 (or_2_out, not_3_out, controlled_buffer_4_out);
  and and_2 (and_2_out, or_2_out, not_2_out);
  not not_2 (not_2_out, controlled_buffer_4_out);
  assign controlled_buffer_3_out = and_5_out ? Register_A_in : 8'bz;  // Controlled_Buffer controlled_buffer_3
  not not_3 (not_3_out, Read);
  assign controlled_buffer_4_out = not_3_out ? Write : 1'bz;  // Controlled_Buffer controlled_buffer_4
  and and_3 (and_3_out, ALU_out_cntl, In_from_condition_block);
  and and_4 (and_4_out, Register_A_out_cntl, In_from_condition_block);
  and and_5 (and_5_out, In_from_condition_block, Write);

  // Notes on the sheet:
  //   Copyright - Ben Oztalay 2008-2009
endmodule

module Jump_P_C__Control (
  input  [7:0] P_C__in,
  input  [7:0] Data_bus_in,
  input  No_jump,
  input  Jump,
  input  In_from_condition_block,
  output Q7,
  output Q6,
  output Q5,
  output Q4,
  output Q3,
  output Q2,
  output Q1,
  output Q0
);

  wire and_1_out, full_adder_1_s, full_adder_2_cout, full_adder_2_s, full_adder_3_cout, full_adder_3_s,
       full_adder_4_cout, full_adder_4_s, full_adder_5_cout, full_adder_5_s, full_adder_6_cout,
       full_adder_6_s, full_adder_7_cout, full_adder_7_s, full_adder_8_cout, full_adder_8_s, not_1_out,
       not_2_out, or_1_out;

  full_adder full_adder_1 (.A(not_1_out), .B(P_C__in[7]), .S(full_adder_1_s), .Cin(full_adder_2_cout));  // open: Cout
  full_adder full_adder_2 (
    .Cout(full_adder_2_cout), .A(not_1_out), .B(P_C__in[6]), .S(full_adder_2_s), .Cin(full_adder_3_cout));
  not not_1 (not_1_out, 1'b1);
  full_adder full_adder_3 (
    .Cout(full_adder_3_cout), .A(not_1_out), .B(P_C__in[5]), .S(full_adder_3_s), .Cin(full_adder_4_cout));
  full_adder full_adder_4 (
    .Cout(full_adder_4_cout), .A(not_1_out), .B(P_C__in[4]), .S(full_adder_4_s), .Cin(full_adder_5_cout));
  or or_1 (or_1_out, No_jump, not_2_out);
  _16_8_MUX u_16_8_mux_1 (
    .B7(full_adder_1_s), .B6(full_adder_2_s), .B5(full_adder_3_s), .B4(full_adder_4_s), .B3(full_adder_5_s),
    .B2(full_adder_6_s), .B1(full_adder_7_s), .B0(full_adder_8_s), .A7(Data_bus_in[7]), .A6(Data_bus_in[6]),
    .A5(Data_bus_in[5]), .A4(Data_bus_in[4]), .A3(Data_bus_in[3]), .A2(Data_bus_in[2]), .A1(Data_bus_in[1]),
    .A0(Data_bus_in[0]), .Q7(Q7), .Q6(Q6), .Q5(Q5), .Q4(Q4), .Q3(Q3), .Q2(Q2), .Q1(Q1), .Q0(Q0),
    .cntl1(or_1_out), .cntl0(and_1_out));
  full_adder full_adder_5 (
    .Cout(full_adder_5_cout), .A(not_1_out), .B(P_C__in[3]), .S(full_adder_5_s), .Cin(full_adder_6_cout));
  full_adder full_adder_6 (
    .Cout(full_adder_6_cout), .A(not_1_out), .B(P_C__in[2]), .S(full_adder_6_s), .Cin(full_adder_7_cout));
  and and_1 (and_1_out, Jump, In_from_condition_block);
  not not_2 (not_2_out, and_1_out);
  full_adder full_adder_7 (
    .Cout(full_adder_7_cout), .A(not_1_out), .B(P_C__in[1]), .S(full_adder_7_s), .Cin(full_adder_8_cout));
  full_adder full_adder_8 (.Cout(full_adder_8_cout), .A(1'b1), .B(P_C__in[0]), .S(full_adder_8_s), .Cin(not_1_out));

  // Notes on the sheet:
  //   Copyright - Ben Oztalay 2008-2009
endmodule

module Condition_Block (
  input  Z,
  input  NZ,
  input  test_Z,
  input  test_NZ,
  output Q
);

  wire and_1_out, and_2_out, and_3_out, not_1_out, not_2_out;

  and and_1 (and_1_out, NZ, test_NZ);
  and and_2 (and_2_out, Z, test_Z);
  not not_1 (not_1_out, test_Z);
  and and_3 (and_3_out, not_1_out, not_2_out);
  or or_1 (Q, and_2_out, and_3_out, and_1_out);
  not not_2 (not_2_out, test_NZ);

  // Notes on the sheet:
  //   Copyright - Ben Oztalay 2008-2009
endmodule

module Pin_Driver (
  input  CLK,
  input  PON_op__sig__in,
  input  CB_in,
  input  [7:0] Data_bus_in,
  output Q7,
  output Q6,
  output Q5,
  output Q4,
  output Q3,
  output Q2,
  output Q1,
  output Q0
);

  wire and_1_out, not_1_out;

  not not_1 (not_1_out, CLK);
  and and_1 (and_1_out, CB_in, PON_op__sig__in, not_1_out);
  Register #(.width(8)) register_1 (
    .D(Data_bus_in), .Q({Q7, Q6, Q5, Q4, Q3, Q2, Q1, Q0}), .clk(and_1_out));  // open: en, clr

  // Notes on the sheet:
  //   Copyright - Ben Oztalay 2008-2009
endmodule
